// Logisim project COMBINATIONALDIVIDER.circ as structural Verilog: 1 circuit, main circuit main
module main (
);

  wire and_1_out, and_2_out, and_3_out, and_4_out, dipswitch_2_p1, dipswitch_2_p2, not_1_out, not_2_out,
       or_1_out, or_2_out, undriven, xor_1_out, xor_2_out;

  // DipSwitch #(.number(4)) dipswitch_1: pin names not known
  // DipSwitch #(.number(3)) dipswitch_2: pin names not known; wires that end beside it: dipswitch_2_p1, dipswitch_2_p2
  not not_1 (not_1_out, dipswitch_2_p2);
  xor xor_1 (xor_1_out, dipswitch_2_p1, not_1_out);
  and and_1 (and_1_out, dipswitch_2_p1, not_1_out);
  xor xor_2 (xor_2_out, xor_1_out, 1'b1);
  and and_2 (and_2_out, xor_1_out, 1'b1);
  not not_2 (not_2_out, undriven);
  or or_1 (or_1_out, and_2_out, and_1_out);
  and and_3 (and_3_out, dipswitch_2_p1, not_2_out);
  and and_4 (and_4_out, xor_2_out, undriven);
  or or_2 (or_2_out, and_3_out, and_4_out);

  // Notes on the sheet:
  //   D3
  //   d0
  //   FA (2's complement)
  //   Signal line (Quotient)
  //   Sum
  //   Cout
  //   Mux
  //   Sum
endmodule
